# Fritzing sketch kv_checker (saved by Fritzing 0.9.9b)
perfboards: 1

parts:
  Mod1 = seeeduino-xiao
  U2 = TCRT5000 [package=THT]
  U3 = LM358 [part_number=LM358 package=dip08]
  R1 = Resistor [tolerance=±1% power=0.25 resistance=2.2k package=THT]
  R2 = Resistor [tolerance=±1% power=0.25 resistance=100 package=THT]
  R3 = TRIMPOT [part_number=10k package=trim_pot_pth]
  Grove1 = Grove 4 Digit Display
  J1 = Power Jack [package=power_jack_pth_lock]
  S3 = Pushbutton [package=THT]
  S1 = Pushbutton [package=THT]
  S2 = Pushbutton [package=THT]
  R4 = Resistor [tolerance=±1% power=0.25 resistance=6.8k package=THT]
  R5 = Resistor [tolerance=±1% power=0.25 resistance=51k package=THT]
  IC1 = LM3480IM4 [part_number=AMS1117 package=sot23-3]

nets:
  N1: Mod1.D3, R4.Pin_0, R5.Pin_0
  N2: Mod1.D4, S3.leg1
  N3: Mod1.D5, S2.leg1
  N4: Mod1.D6, S1.leg1
  N5: Mod1.D7, Grove1.CLK
  N6: Mod1.D8, Grove1.DIO
  N7: Mod1.D9, U3.G$1_OUT
  3V3: Mod1.3V3, U3.G$1_V+, R1.Pin_1, R2.Pin_1, R3.CW, Grove1.VCC
  GND: Mod1.GND, U2.Pin_2, U2.Pin_3, U3.G$1_V-, R3.CCW, Grove1.GND, J1.GND, S3.leg0, S1.leg0, S2.leg0, R4.Pin_1, IC1.GND
  N8: Mod1.5V, IC1.OUT
  N9: U2.Pin_1, U3.G$1_-IN, R1.Pin_0
  N10: U2.Pin_4, R2.Pin_0
  N11: U3.G$1_+IN, R3.WIPER
  N12: J1.PWR, R5.Pin_1, IC1.IN

custom parts:
  seeeduino-xiao: Seeeduino XIAO processor board.
  TCRT5000: TCRT5000 optical reflective sensor
